// Logisim project beag_task_b.circ as structural Verilog: 1 circuit, main circuit main
module main (
);

  wire and_2_out, and_3_out, and_4_out, and_6_out, and_7_out, and_8_out, and_9_out, and_10_out, and_11_out,
       and_12_out, clock_1_out, clock_2_out, clock_3_out, clock_4_out, clock_5_out, clock_6_out, clock_7_out,
       clock_8_out, clock_9_out, clock_10_out, clock_11_out, clock_12_out, clock_13_out, comparator_2_eq,
       comparator_3_eq, comparator_4_eq, comparator_5_eq, comparator_6_eq, comparator_7_eq, decoder_1_out1,
       decoder_1_out2, decoder_1_out3, decoder_1_out4, decoder_1_out5, decoder_1_out6, decoder_1_out7,
       decoder_2_out0, decoder_2_out1, decoder_2_out2, decoder_2_out3, decoder_2_out6, decoder_2_out8,
       decoder_2_out13, decoder_2_out14, decoder_2_out15, execute, fetch, ImmExt, keyboard_1_avail, MemR,
       MemW, not_2_out, XeqY, XltY;
  wire [1:0] PCsel, SrcSel;
  wire [2:0] ArithCode, Dsel, Xsel, Ysel;
  wire [2:2] not_1_out, or_4_out;
  wire [6:0] keyboard_1_data, multiplexer_6_out;
  wire [7:0] Imm;
  wire [13:0] bit_extender_4_out;
  wire [15:0] adder_1_out, adder_2_out, adder_3_out, bit_extender_1_out, bit_extender_2_out,
       bit_extender_3_out, controlled_buffer_1_out, divider_1_out, divider_1_rem, IR_q, multiplexer_1_out,
       multiplexer_2_out, multiplexer_3_out, multiplexer_5_out, multiplexer_8_out, multiplexer_9_out,
       multiplier_1_out, PC, ram_1_dout, register_1_q, register_2_q, register_3_q, register_4_q,
       register_5_q, register_6_q, register_7_q, register_8_q, rom_1_data, subtractor_1_out;
  wire [15:7] multiplexer_6_out_2;
  wire [15:8] multiplexer_4_out;

  assign bit_extender_1_out = {{8{Imm[7]}}, Imm};  // Bit_Extender bit_extender_1
  Multiplexer #(.width(16)) multiplexer_1 (
    .in0({Imm, multiplexer_8_out[7:0]}), .in1(bit_extender_1_out), .out(multiplexer_1_out), .sel(ImmExt));
  Adder #(.width(16)) adder_1 (.a(PC), .b(16'h1), .out(adder_1_out));  // open: cin, cout
  Adder #(.width(16)) adder_2 (.a(PC), .b(bit_extender_1_out), .out(adder_2_out));  // open: cin, cout
  Register #(.width(16)) u_PC (.D(multiplexer_2_out), .en(execute), .clk(clock_1_out), .Q(PC));  // open: clr
  Multiplexer #(.select(2), .width(16)) multiplexer_2 (
    .in0(adder_1_out), .in1(adder_2_out), .in2(multiplexer_8_out), .out(multiplexer_2_out), .sel(PCsel));  // open: in3
  Clock clock_1 (.out(clock_1_out));
  Multiplexer #(.select(2), .width(16)) multiplexer_3 (
    .in0(multiplexer_8_out), .in1(controlled_buffer_1_out), .in2(multiplexer_1_out), .in3(adder_1_out),
    .out(multiplexer_3_out), .sel(SrcSel));
  Decoder #(.enable("false"), .select(3)) decoder_1 (
    .out1(decoder_1_out1), .out2(decoder_1_out2), .out3(decoder_1_out3), .out4(decoder_1_out4),
    .out5(decoder_1_out5), .out6(decoder_1_out6), .out7(decoder_1_out7), .sel(Dsel));  // open: out0
  Register #(.width(16)) register_1 (
    .D(multiplexer_3_out), .en(decoder_1_out2), .clk(clock_2_out), .Q(register_1_q));  // open: clr
  Clock clock_2 (.out(clock_2_out));
  Register #(.width(16)) register_2 (
    .D(multiplexer_3_out), .en(decoder_1_out4), .clk(clock_3_out), .Q(register_2_q));  // open: clr
  Clock clock_3 (.out(clock_3_out));
  Register #(.width(16)) register_3 (
    .D(multiplexer_3_out), .en(decoder_1_out6), .clk(clock_4_out), .Q(register_3_q));  // open: clr
  Clock clock_4 (.out(clock_4_out));
  Register #(.width(16)) IR (.D(controlled_buffer_1_out), .en(fetch), .clk(clock_5_out), .Q(IR_q));  // open: clr
  Clock clock_5 (.out(clock_5_out));
  D_Flip_Flop d_ff_1 (.D(fetch), .clk(clock_6_out), .Q(execute), .Qn(fetch));  // open: preset, reset
  Clock clock_6 (.out(clock_6_out));
  Register #(.width(16)) register_4 (
    .D(multiplexer_3_out), .en(decoder_1_out1), .clk(clock_7_out), .Q(register_4_q));  // open: clr
  Clock clock_7 (.out(clock_7_out));
  Register #(.width(16)) register_5 (
    .D(multiplexer_3_out), .en(decoder_1_out3), .clk(clock_8_out), .Q(register_5_q));  // open: clr
  Clock clock_8 (.out(clock_8_out));
  Register #(.width(16)) register_6 (
    .D(multiplexer_3_out), .en(decoder_1_out5), .clk(clock_9_out), .Q(register_6_q));  // open: clr
  Clock clock_9 (.out(clock_9_out));
  Register #(.width(16)) register_7 (
    .D(multiplexer_3_out), .en(decoder_1_out7), .clk(clock_10_out), .Q(register_7_q));  // open: clr
  Clock clock_10 (.out(clock_10_out));
  Multiplexer #(.width(16)) multiplexer_4 (
    .in0(IR_q), .in1({16{1'b0}}),
    .out({multiplexer_4_out[15:14], ArithCode[1:0], multiplexer_4_out[11:8], Imm}), .sel(fetch));
  Multiplexer #(.select(3), .width(16)) multiplexer_5 (
    .in0({16{1'b0}}), .in1(register_4_q), .in2(register_1_q), .in3(register_5_q), .in4(register_2_q),
    .in5(register_6_q), .in6(register_3_q), .in7(register_7_q), .out(multiplexer_5_out), .sel(Xsel));
  Multiplexer #(.select(3), .width(16)) multiplexer_6 (
    .in0({16{1'b0}}), .in1(register_4_q), .in2(register_1_q), .in3(register_5_q), .in4(register_2_q),
    .in5(register_6_q), .in6(register_3_q), .in7(register_7_q),
    .out({multiplexer_6_out_2, multiplexer_6_out}), .sel(Ysel));
  not not_1 (not_1_out[2], multiplexer_4_out[15]);
  Decoder #(.enable("false"), .select(4)) decoder_2 (
    .out0(decoder_2_out0), .out1(decoder_2_out1), .out2(decoder_2_out2), .out3(decoder_2_out3),
    .out4(PCsel[1]), .out5(MemW), .out6(decoder_2_out6), .out7(ArithCode[2]), .out8(decoder_2_out8),
    .out9(ImmExt), .out13(decoder_2_out13), .out14(decoder_2_out14), .out15(decoder_2_out15),
    .sel({multiplexer_4_out[15:14], ArithCode[1:0]}));  // open: out10, out11, out12
  not not_2 (not_2_out, XeqY);
  assign Ysel = Imm[2:0] & {3{not_1_out[2]}};  // AND_Gate and_1, 3 bits wide
  Multiplexer #(.width(3)) multiplexer_7 (
    .in0(Imm[6:4]), .in1(multiplexer_4_out[10:8]), .out(Xsel), .sel(multiplexer_4_out[15]));
  and and_2 (and_2_out, decoder_2_out13, not_2_out);
  and and_3 (and_3_out, decoder_2_out14, XeqY);
  and and_4 (and_4_out, decoder_2_out15, XltY);
  Adder #(.width(16)) adder_3 (
    .a(multiplexer_5_out), .b({multiplexer_6_out_2, multiplexer_6_out}), .out(adder_3_out));  // open: cin, cout
  Subtractor #(.width(16)) subtractor_1 (
    .a(multiplexer_5_out), .b({multiplexer_6_out_2, multiplexer_6_out}), .out(subtractor_1_out));  // open: bin, bout
  Multiplier #(.mode("twosComplement"), .width(16)) multiplier_1 (
    .a(multiplexer_5_out), .b({multiplexer_6_out_2, multiplexer_6_out}), .out(multiplier_1_out));  // open: cin, cout
  Divider #(.mode("twosComplement"), .width(16)) divider_1 (
    .a(multiplexer_5_out), .b({multiplexer_6_out_2, multiplexer_6_out}), .out(divider_1_out),
    .rem(divider_1_rem));  // open: upper
  Comparator #(.width(16)) comparator_1 (
    .a(multiplexer_5_out), .b({multiplexer_6_out_2, multiplexer_6_out}), .eq(XeqY), .lt(XltY));  // open: gt
  or or_1 (PCsel[0], and_2_out, and_3_out, and_4_out);
  Multiplexer #(.select(3), .width(16)) multiplexer_8 (
    .in0(adder_3_out), .in1(subtractor_1_out), .in2(multiplier_1_out), .in3(divider_1_out),
    .in7(divider_1_rem), .out(multiplexer_8_out), .sel(ArithCode));  // open: in4, in5, in6
  or or_2 (SrcSel[0], PCsel[1], decoder_2_out6);
  or or_3 (SrcSel[1], decoder_2_out8, ImmExt, PCsel[1]);
  assign Dsel = multiplexer_4_out[10:8] & {3{or_4_out[2]}};  // AND_Gate and_5, 3 bits wide
  or or_4 (or_4_out[2], ArithCode[2], decoder_2_out0, PCsel[1], decoder_2_out1, decoder_2_out2, decoder_2_out3, decoder_2_out6, decoder_2_out8, ImmExt);
  Multiplexer #(.width(16)) multiplexer_9 (.in0(multiplexer_5_out), .in1(PC), .out(multiplexer_9_out), .sel(fetch));
  or or_5 (MemR, decoder_2_out6, fetch);
  Comparator #(.width(4)) comparator_2 (
    .a(multiplexer_9_out[15:12]), .b(4'b0000), .eq(comparator_2_eq));  // open: gt, lt
  and and_6 (and_6_out, comparator_2_eq, MemR);
  Comparator #(.width(4)) comparator_3 (
    .a(multiplexer_9_out[15:12]), .b(4'b0010), .eq(comparator_3_eq));  // open: gt, lt
  and and_7 (and_7_out, comparator_3_eq, MemW);
  and and_8 (and_8_out, comparator_3_eq, MemR);
  Comparator #(.width(16)) comparator_4 (.a(multiplexer_9_out), .b(16'h4000), .eq(comparator_4_eq));  // open: gt, lt
  Comparator #(.width(16)) comparator_5 (.a(multiplexer_9_out), .b(16'h4002), .eq(comparator_5_eq));  // open: gt, lt
  Comparator #(.width(16)) comparator_6 (.a(multiplexer_9_out), .b(16'h4001), .eq(comparator_6_eq));  // open: gt, lt
  ROM #(.addrWidth(12), .dataWidth(16)) rom_1 (.addr(multiplexer_9_out[11:0]), .data(rom_1_data));
  RAM #(.addrWidth(12), .dataWidth(16), .enables("line")) ram_1 (
    .addr(multiplexer_9_out[11:0]), .we(and_7_out), .clk(clock_11_out),
    .din({multiplexer_6_out_2, multiplexer_6_out}), .dout(ram_1_dout));
  Clock clock_11 (.out(clock_11_out));
  and and_9 (and_9_out, comparator_4_eq, MemW);
  Clock clock_12 (.out(clock_12_out));
  and and_10 (and_10_out, comparator_5_eq, MemR);
  and and_11 (and_11_out, comparator_6_eq, MemR);
  TTY tty_1 (.data(multiplexer_6_out), .clk(clock_12_out), .we(and_9_out));  // open: clr
  Clock clock_13 (.out(clock_13_out));
  Keyboard keyboard_1 (
    .clk(clock_13_out), .re(and_10_out), .avail(keyboard_1_avail), .data(keyboard_1_data));  // open: clr
  assign controlled_buffer_1_out = and_6_out ? rom_1_data : 16'bz;  // Controlled_Buffer controlled_buffer_1
  assign controlled_buffer_1_out = and_8_out ? ram_1_dout : 16'bz;  // Controlled_Buffer controlled_buffer_2
  assign bit_extender_2_out = {{9{1'b0}}, keyboard_1_data};  // Bit_Extender bit_extender_2
  assign controlled_buffer_1_out = and_10_out ? bit_extender_2_out : 16'bz;  // Controlled_Buffer controlled_buffer_3
  assign bit_extender_3_out = {{15{1'b0}}, keyboard_1_avail};  // Bit_Extender bit_extender_3
  assign controlled_buffer_1_out = and_11_out ? bit_extender_3_out : 16'bz;  // Controlled_Buffer controlled_buffer_4
  Register #(.width(16)) register_8 (
    .D(controlled_buffer_1_out), .en(and_12_out), .clk(clock_12_out), .Q(register_8_q));  // open: clr
  Comparator #(.width(16)) comparator_7 (.a(multiplexer_9_out), .b(16'h4003), .eq(comparator_7_eq));  // open: gt, lt
  and and_12 (and_12_out, comparator_7_eq, MemW);
  Bit_Extender #(.in_width(16), .out_width(14)) bit_extender_4 (.in(register_8_q), .out(bit_extender_4_out));
  // Buzzer #(.vol_width(16)) buzzer_1: pin names not known; wires that end beside it: bit_extender_4_out, 1'b1

  // Notes on the sheet:
  //   R2
  //   R4
  //   R6
  //   R0
  //   Fetch / Execute FSM
  //   R1
  //   R3
  //   R5
  //   R7
  //   Y
  //   X
  //   Dst
  //   I/R
  //   OpCode
  //   Beag Computer (von Neumann Architecture)
  //   X
  //   Y
  //   ALU
  //   Instruction decoder
  //   Data In
  //   Address
  //   Data Out
  //   contents of rom_1 (hex, n*v repeats v):
  //   9100 8140 9201 8240 9302 8340 9400 8420 9500 6620 e6ff 6630 9701 1776 e706 5046 9701 557 447 e0f6
  //   e507 9701 1557 1447 6640 5016 e0fa e000
  //   Display
  //   Keyboard
endmodule
